# Fritzing sketch Test_Servo (saved by Fritzing 0.9.3b)
breadboards: 1

parts:
  Componente1 = Arduino Uno (Rev3)
  J1 = Basic Servo
  J2 = Basic Servo

nets:
  N1: Componente1.D5_PWM, J1.pulse
  N2: Componente1.D6_PWM, J2.pulse
  VCC: Componente1.5V, J1.vcc, J2.vcc
  GND: Componente1.GND, J1.gnd, J2.gnd
