# Fritzing sketch Test_Servo_with_BlueTooth (saved by Fritzing 0.9.3b)
breadboards: 1

parts:
  Componente1 = Arduino Uno (Rev3)
  J1 = Basic Servo
  J2 = Basic Servo
  Componente2 = Bluetooth HC-05 Macho

nets:
  N1: Componente1.D0/RX, Componente2.TXD
  N2: Componente1.D1/TX, Componente2.RXD
  N3: Componente1.D5_PWM, J1.pulse
  N4: Componente1.D6_PWM, J2.pulse
  VCC: Componente1.5V, J1.vcc, J2.vcc, Componente2.VCC
  GND: Componente1.GND, J1.gnd, J2.gnd, Componente2.GND
